// Digital circuit 8910_complete.dig as structural Verilog
module _8910_complete (
);

  // dac_decoder_7400 dac_decoder_7400_1: pin names not known
  // dac_decoder_7400 dac_decoder_7400_2: pin names not known
  // dac_decoder_7400 dac_decoder_7400_3: pin names not known
endmodule
