// Digital circuit addr_decoder.dig as structural Verilog
module addr_decoder (
  input  D3_LATCH,
  input  D2_LATCH,
  input  D1_LATCH,
  input  D0_LATCH,
  input  INTERNAL_SEL,
  output SEL_R17,
  output SEL_R16,
  output SEL_R15,
  output SEL_R14
);

  wire not_1_out, not_2_out, not_3_out, not_4_out, not_5_out, or_1_out, or_2_out, or_3_out, or_4_out,
       or_10_out, or_11_out;

  not not_1 (not_1_out, D3_LATCH);
  not not_2 (not_2_out, D2_LATCH);
  not not_3 (not_3_out, D1_LATCH);
  not not_4 (not_4_out, D0_LATCH);
  not not_5 (not_5_out, INTERNAL_SEL);
  or or_1 (or_1_out, not_1_out, not_2_out, not_3_out);
  or or_2 (or_2_out, not_1_out, not_2_out, not_3_out);
  or or_3 (or_3_out, not_1_out, not_2_out, D2_LATCH);
  or or_4 (or_4_out, not_1_out, not_2_out, D2_LATCH);
  // Or or_5 is placed but not wired
  // Or or_6 is placed but not wired
  // Or or_7 is placed but not wired
  // Or or_8 is placed but not wired
  // Or or_9 is placed but not wired
  or or_10 (or_10_out, or_1_out, not_4_out, not_5_out);
  or or_11 (or_11_out, or_2_out, D0_LATCH, not_5_out);
  or or_12 (SEL_R15, or_3_out, not_4_out, not_5_out);
  or or_13 (SEL_R14, or_4_out, D1_LATCH, not_5_out);
  // Or or_14 is placed but not wired
  // Or or_15 is placed but not wired
  // Or or_16 is placed but not wired
  // Or or_17 is placed but not wired
  // Or or_18 is placed but not wired
  not not_6 (SEL_R17, or_10_out);
  not not_7 (SEL_R16, or_11_out);
endmodule
