// Digital circuit dac_decoder_7400_new.dig as structural Verilog
module dac_decoder_7400_new (
  input  OE,
  input  A0,
  input  A1,
  input  A2,
  input  A3,
  output Y7,
  output Y6,
  output Y5,
  output Y4,
  output Y3,
  output Y2,
  output Y1,
  output Y0
);

  wire _7408_1_pin2, _7408_2_pin2, _7408_3_pin2, _7408_4_pin2, _7432_1_pin4, _7432_1_pin5, _7432_1_pin6,
       _7432_1_pin9, _7432_1_pin10, _7432_1_pin12, _74238_1_pin12, _74238_1_pin13, _74238_1_pin14,
       _74238_1_pin15, _744075_1_pin1, _744075_1_pin2, _744075_1_pin3, _744075_1_pin4, _744075_1_pin5,
       _744075_1_pin6, _744075_1_pin8, _744075_1_pin11, _744075_1_pin12, _744075_1_pin13, _744075_2_pin1,
       _744075_2_pin2, _744075_2_pin3, _744075_2_pin4, _744075_2_pin5, _744075_2_pin8, _744075_2_pin9,
       _744075_2_pin10, _744075_2_pin11, _744075_2_pin12, _744075_2_pin13, _744075_3_pin1, _744075_3_pin2,
       _744075_3_pin3, _744075_3_pin4, _744075_3_pin5, _744075_3_pin8, _744075_3_pin11, _744075_3_pin12,
       _744075_3_pin13, _744075_4_pin1, _744075_4_pin2, _744075_4_pin3, _744075_4_pin4, _744075_4_pin5,
       _744075_4_pin11, _744075_4_pin12, _744075_4_pin13;

  _744075 _744075_1 (
    .pin1(_744075_1_pin1), .pin2(_744075_1_pin2), .pin3(_744075_1_pin3), .pin4(_744075_1_pin4),
    .pin5(_744075_1_pin5), .pin6(_744075_1_pin6), .pin7(1'b0), .pin8(_744075_1_pin8), .pin9(Y3), .pin10(Y5),
    .pin11(_744075_1_pin11), .pin12(_744075_1_pin12), .pin13(_744075_1_pin13), .pin14(1'b1));
  _744075 _744075_2 (
    .pin1(_744075_2_pin1), .pin2(_744075_2_pin2), .pin3(_744075_2_pin3), .pin4(_744075_2_pin4),
    .pin5(_744075_2_pin5), .pin6(_744075_1_pin1), .pin7(1'b0), .pin8(_744075_2_pin8), .pin9(_744075_2_pin9),
    .pin10(_744075_2_pin10), .pin11(_744075_2_pin11), .pin12(_744075_2_pin12), .pin13(_744075_2_pin13),
    .pin14(1'b1));
  _744075 _744075_3 (
    .pin1(_744075_3_pin1), .pin2(_744075_3_pin2), .pin3(_744075_3_pin3), .pin4(_744075_3_pin4),
    .pin5(_744075_3_pin5), .pin6(Y1), .pin7(1'b0), .pin8(_744075_3_pin8), .pin9(_744075_3_pin5),
    .pin10(_744075_3_pin4), .pin11(_744075_3_pin11), .pin12(_744075_3_pin12), .pin13(_744075_3_pin13),
    .pin14(1'b1));
  _7432 _7432_1 (
    .pin1(_744075_2_pin9), .pin2(_744075_2_pin10), .pin3(Y2), .pin4(_7432_1_pin4), .pin5(_7432_1_pin5),
    .pin6(_7432_1_pin6), .pin7(1'b0), .pin8(Y6), .pin9(_7432_1_pin9), .pin10(_7432_1_pin10), .pin11(Y4),
    .pin12(_7432_1_pin12), .pin13(_744075_1_pin6), .pin14(1'b1));
  _744075 _744075_4 (
    .pin1(_744075_4_pin1), .pin2(_744075_4_pin2), .pin3(_744075_4_pin3), .pin4(_744075_4_pin4),
    .pin5(_744075_4_pin5), .pin6(_744075_4_pin2), .pin7(1'b0), .pin8(_7432_1_pin6), .pin9(Y0),
    .pin10(_744075_4_pin1), .pin11(_744075_4_pin11), .pin12(_744075_4_pin12), .pin13(_744075_4_pin13),
    .pin14(1'b1));
  _7408 _7408_1 (
    .pin1(1'b1), .pin2(_7408_1_pin2), .pin3(_744075_1_pin3), .pin4(1'b1), .pin5(_7408_1_pin2),
    .pin6(_744075_2_pin13), .pin7(1'b0), .pin8(_744075_3_pin1), .pin9(_7408_1_pin2), .pin10(1'b1),
    .pin11(_744075_2_pin4), .pin12(_7408_1_pin2), .pin13(A0), .pin14(1'b1));
  _7408 _7408_2 (
    .pin1(1'b1), .pin2(_7408_2_pin2), .pin3(_744075_1_pin11), .pin4(1'b1), .pin5(_7408_2_pin2),
    .pin6(_744075_2_pin3), .pin7(1'b0), .pin8(_744075_2_pin1), .pin9(_7408_2_pin2), .pin10(1'b1),
    .pin11(_744075_1_pin4), .pin12(_7408_2_pin2), .pin13(A0), .pin14(1'b1));
  _7408 _7408_3 (
    .pin1(1'b1), .pin2(_7408_3_pin2), .pin3(_7432_1_pin9), .pin4(1'b1), .pin5(_7408_3_pin2),
    .pin6(_744075_1_pin5), .pin7(1'b0), .pin8(_744075_1_pin2), .pin9(_7408_3_pin2), .pin10(1'b1),
    .pin11(_744075_1_pin12), .pin12(_7408_3_pin2), .pin13(A0), .pin14(1'b1));
  _7408 _7408_4 (
    .pin1(1'b1), .pin2(_7408_4_pin2), .pin3(Y7), .pin4(1'b1), .pin5(_7408_4_pin2), .pin6(_744075_1_pin13),
    .pin7(1'b0), .pin8(_7432_1_pin12), .pin9(_7408_4_pin2), .pin10(1'b1), .pin11(_7432_1_pin10),
    .pin12(_7408_4_pin2), .pin13(A0), .pin14(1'b1));
  _74238 _74238_1 (
    .pin1(A1), .pin2(A2), .pin3(A3), .pin4(1'b0), .pin5(1'b0), .pin6(OE), .pin7(_7408_4_pin2), .pin8(1'b0),
    .pin9(_7408_3_pin2), .pin10(_7408_2_pin2), .pin11(_7408_1_pin2), .pin12(_74238_1_pin12),
    .pin13(_74238_1_pin13), .pin14(_74238_1_pin14), .pin15(_74238_1_pin15), .pin16(1'b1));
  _7408 _7408_5 (
    .pin1(1'b1), .pin2(_74238_1_pin13), .pin3(_744075_4_pin13), .pin4(1'b1), .pin5(_74238_1_pin14),
    .pin6(_744075_3_pin11), .pin7(1'b0), .pin8(_744075_4_pin12), .pin9(_74238_1_pin14), .pin10(A0),
    .pin11(_744075_4_pin11), .pin12(A0), .pin13(_74238_1_pin15), .pin14(1'b1));
  _7408 _7408_6 (
    .pin1(A0), .pin2(_7408_1_pin2), .pin3(_744075_4_pin4), .pin4(1'b1), .pin5(_74238_1_pin13),
    .pin6(_744075_2_pin11), .pin7(1'b0), .pin8(_744075_3_pin12), .pin9(_74238_1_pin13), .pin10(A0),
    .pin11(_744075_4_pin5), .pin12(_74238_1_pin12), .pin13(1'b1), .pin14(1'b1));
  _7408 _7408_7 (
    .pin1(A0), .pin2(_7408_2_pin2), .pin3(_744075_3_pin2), .pin4(A0), .pin5(_74238_1_pin12),
    .pin6(_744075_2_pin12), .pin7(1'b0), .pin8(_744075_3_pin13), .pin9(_74238_1_pin12), .pin10(1'b1),
    .pin11(_744075_4_pin3), .pin12(_7408_2_pin2), .pin13(1'b1), .pin14(1'b1));
  _7408 _7408_8 (
    .pin1(A0), .pin2(_7408_3_pin2), .pin3(_744075_2_pin2), .pin4(A0), .pin5(_7408_3_pin2),
    .pin6(_7432_1_pin5), .pin7(1'b0), .pin8(_744075_2_pin5), .pin9(1'b1), .pin10(_74238_1_pin12),
    .pin11(_744075_3_pin8), .pin12(_7408_3_pin2), .pin13(1'b1), .pin14(1'b1));
  _7408 _7408_9 (
    .pin1(A0), .pin2(_7408_4_pin2), .pin3(_744075_1_pin8), .pin4(A0), .pin5(_7408_4_pin2),
    .pin6(_744075_3_pin3), .pin7(1'b0), .pin8(_7432_1_pin4), .pin9(_7408_4_pin2), .pin10(1'b1),
    .pin11(_744075_2_pin8), .pin12(_7408_4_pin2), .pin13(1'b1), .pin14(1'b1));

  // Notes on the sheet:
  //   Out6
  //   Out7
  //   Out4
  //   Out5
  //   Out2
  //   Out3
  //   Out0
  //   Out1
  //   Bottom row=in, top row=out
  //   Bit 7
  //   74HC4075 triple 3-input OR x4
  //   74HC32 quad 2-input OR x1
  //   74HC08 quad 2-input AND x9
  //   74HC238 3 to 8 decoder x1
endmodule
