// Digital circuit dac_decoder_new.dig as structural Verilog
module dac_decoder_new (
  input  In3,
  input  In2,
  input  In1,
  input  In0,
  input  OE,
  input  A0,
  input  A1,
  input  A2,
  input  A3,
  output Out0,
  output Out1,
  output Out2,
  output Out3,
  output Out4,
  output Out5,
  output Out6,
  output Out7,
  output Y7,
  output Y6,
  output Y5,
  output Y4,
  output Y3,
  output Y2,
  output Y1,
  output Y0
);

  wire _7408_1_pin2, _7408_2_pin2, _7408_3_pin2, _7408_4_pin2, _7432_1_pin4, _7432_1_pin5, _7432_1_pin6,
       _7432_1_pin9, _7432_1_pin10, _7432_1_pin12, _74238_1_pin12, _74238_1_pin13, _74238_1_pin14,
       _74238_1_pin15, _744075_1_pin1, _744075_1_pin2, _744075_1_pin3, _744075_1_pin4, _744075_1_pin5,
       _744075_1_pin6, _744075_1_pin8, _744075_1_pin11, _744075_1_pin12, _744075_1_pin13, _744075_2_pin1,
       _744075_2_pin2, _744075_2_pin3, _744075_2_pin4, _744075_2_pin5, _744075_2_pin8, _744075_2_pin9,
       _744075_2_pin10, _744075_2_pin11, _744075_2_pin12, _744075_2_pin13, _744075_3_pin1, _744075_3_pin2,
       _744075_3_pin3, _744075_3_pin4, _744075_3_pin5, _744075_3_pin8, _744075_3_pin11, _744075_3_pin12,
       _744075_3_pin13, _744075_4_pin1, _744075_4_pin2, _744075_4_pin3, _744075_4_pin4, _744075_4_pin5,
       _744075_4_pin11, _744075_4_pin12, _744075_4_pin13, and_1_out, and_2_out, and_3_out, and_4_out,
       and_5_out, and_6_out, and_7_out, and_8_out, and_9_out, and_10_out, and_11_out, and_12_out, and_13_out,
       and_14_out, and_15_out, and_16_out, and_17_out, and_18_out, and_19_out, and_20_out, and_21_out,
       and_22_out, and_23_out, and_24_out, and_25_out, and_26_out, and_27_out, and_28_out, and_29_out,
       and_30_out, and_31_out, and_32_out, and_33_out, and_34_out, and_35_out, and_36_out, and_37_out,
       and_38_out, and_39_out, and_40_out, and_41_out, and_42_out, and_43_out, and_44_out, and_45_out,
       and_46_out, and_47_out, not_1_out, not_2_out, not_3_out, not_4_out, not_5_out, not_6_out, not_7_out,
       not_8_out, or_4_out, or_7_out, or_10_out, or_11_out, or_12_out, or_13_out, or_14_out, or_15_out,
       or_16_out;

  _744075 _744075_1 (
    .pin1(_744075_1_pin1), .pin2(_744075_1_pin2), .pin3(_744075_1_pin3), .pin4(_744075_1_pin4),
    .pin5(_744075_1_pin5), .pin6(_744075_1_pin6), .pin7(1'b0), .pin8(_744075_1_pin8), .pin9(Y3), .pin10(Y5),
    .pin11(_744075_1_pin11), .pin12(_744075_1_pin12), .pin13(_744075_1_pin13), .pin14(1'b1));
  _744075 _744075_2 (
    .pin1(_744075_2_pin1), .pin2(_744075_2_pin2), .pin3(_744075_2_pin3), .pin4(_744075_2_pin4),
    .pin5(_744075_2_pin5), .pin6(_744075_1_pin1), .pin7(1'b0), .pin8(_744075_2_pin8), .pin9(_744075_2_pin9),
    .pin10(_744075_2_pin10), .pin11(_744075_2_pin11), .pin12(_744075_2_pin12), .pin13(_744075_2_pin13),
    .pin14(1'b1));
  _744075 _744075_3 (
    .pin1(_744075_3_pin1), .pin2(_744075_3_pin2), .pin3(_744075_3_pin3), .pin4(_744075_3_pin4),
    .pin5(_744075_3_pin5), .pin6(Y1), .pin7(1'b0), .pin8(_744075_3_pin8), .pin9(_744075_3_pin5),
    .pin10(_744075_3_pin4), .pin11(_744075_3_pin11), .pin12(_744075_3_pin12), .pin13(_744075_3_pin13),
    .pin14(1'b1));
  _7432 _7432_1 (
    .pin1(_744075_2_pin9), .pin2(_744075_2_pin10), .pin3(Y2), .pin4(_7432_1_pin4), .pin5(_7432_1_pin5),
    .pin6(_7432_1_pin6), .pin7(1'b0), .pin8(Y6), .pin9(_7432_1_pin9), .pin10(_7432_1_pin10), .pin11(Y4),
    .pin12(_7432_1_pin12), .pin13(_744075_1_pin6), .pin14(1'b1));
  _744075 _744075_4 (
    .pin1(_744075_4_pin1), .pin2(_744075_4_pin2), .pin3(_744075_4_pin3), .pin4(_744075_4_pin4),
    .pin5(_744075_4_pin5), .pin6(_744075_4_pin2), .pin7(1'b0), .pin8(_7432_1_pin6), .pin9(Y0),
    .pin10(_744075_4_pin1), .pin11(_744075_4_pin11), .pin12(_744075_4_pin12), .pin13(_744075_4_pin13),
    .pin14(1'b1));
  not not_1 (not_1_out, In3);
  not not_2 (not_2_out, In2);
  not not_3 (not_3_out, In1);
  not not_4 (not_4_out, In0);
  or or_1 (Out2, or_12_out, or_4_out);
  or or_2 (Out4, and_27_out, or_10_out);
  or or_3 (Out3, and_22_out, and_26_out, or_11_out);
  or or_4 (or_4_out, and_30_out, and_36_out, and_43_out);
  or or_5 (Out1, or_14_out, and_24_out, or_13_out);
  or or_6 (Out0, or_16_out, or_7_out, or_15_out);
  or or_7 (or_7_out, and_1_out, and_23_out);
  _7408 _7408_1 (
    .pin1(1'b1), .pin2(_7408_1_pin2), .pin3(_744075_1_pin3), .pin4(1'b1), .pin5(_7408_1_pin2),
    .pin6(_744075_2_pin13), .pin7(1'b0), .pin8(_744075_3_pin1), .pin9(_7408_1_pin2), .pin10(1'b1),
    .pin11(_744075_2_pin4), .pin12(_7408_1_pin2), .pin13(A0), .pin14(1'b1));
  _7408 _7408_2 (
    .pin1(1'b1), .pin2(_7408_2_pin2), .pin3(_744075_1_pin11), .pin4(1'b1), .pin5(_7408_2_pin2),
    .pin6(_744075_2_pin3), .pin7(1'b0), .pin8(_744075_2_pin1), .pin9(_7408_2_pin2), .pin10(1'b1),
    .pin11(_744075_1_pin4), .pin12(_7408_2_pin2), .pin13(A0), .pin14(1'b1));
  _7408 _7408_3 (
    .pin1(1'b1), .pin2(_7408_3_pin2), .pin3(_7432_1_pin9), .pin4(1'b1), .pin5(_7408_3_pin2),
    .pin6(_744075_1_pin5), .pin7(1'b0), .pin8(_744075_1_pin2), .pin9(_7408_3_pin2), .pin10(1'b1),
    .pin11(_744075_1_pin12), .pin12(_7408_3_pin2), .pin13(A0), .pin14(1'b1));
  _7408 _7408_4 (
    .pin1(1'b1), .pin2(_7408_4_pin2), .pin3(Y7), .pin4(1'b1), .pin5(_7408_4_pin2), .pin6(_744075_1_pin13),
    .pin7(1'b0), .pin8(_7432_1_pin12), .pin9(_7408_4_pin2), .pin10(1'b1), .pin11(_7432_1_pin10),
    .pin12(_7408_4_pin2), .pin13(A0), .pin14(1'b1));
  _74238 _74238_1 (
    .pin1(A1), .pin2(A2), .pin3(A3), .pin4(1'b0), .pin5(1'b0), .pin6(OE), .pin7(_7408_4_pin2), .pin8(1'b0),
    .pin9(_7408_3_pin2), .pin10(_7408_2_pin2), .pin11(_7408_1_pin2), .pin12(_74238_1_pin12),
    .pin13(_74238_1_pin13), .pin14(_74238_1_pin14), .pin15(_74238_1_pin15), .pin16(1'b1));
  not not_5 (not_5_out, not_1_out);
  not not_6 (not_6_out, not_2_out);
  not not_7 (not_7_out, not_3_out);
  not not_8 (not_8_out, not_4_out);
  or or_8 (Out6, and_40_out, and_47_out);
  or or_9 (Out5, and_33_out, and_39_out, and_46_out);
  or or_10 (or_10_out, and_32_out, and_38_out, and_45_out);
  or or_11 (or_11_out, and_31_out, and_37_out, and_44_out);
  or or_12 (or_12_out, and_14_out, and_21_out, and_25_out);
  or or_13 (or_13_out, and_29_out, and_35_out, and_42_out);
  or or_14 (or_14_out, and_6_out, and_13_out, and_20_out);
  or or_15 (or_15_out, and_28_out, and_34_out, and_41_out);
  or or_16 (or_16_out, and_5_out, and_12_out, and_19_out);
  and and_1 (and_1_out, not_8_out, and_2_out);
  and and_2 (and_2_out, and_3_out, not_3_out);
  and and_3 (and_3_out, not_1_out, not_2_out);
  _7408 _7408_5 (
    .pin1(1'b1), .pin2(_74238_1_pin13), .pin3(_744075_4_pin13), .pin4(1'b1), .pin5(_74238_1_pin14),
    .pin6(_744075_3_pin11), .pin7(1'b0), .pin8(_744075_4_pin12), .pin9(_74238_1_pin14), .pin10(A0),
    .pin11(_744075_4_pin11), .pin12(A0), .pin13(_74238_1_pin15), .pin14(1'b1));
  _7408 _7408_6 (
    .pin1(A0), .pin2(_7408_1_pin2), .pin3(_744075_4_pin4), .pin4(1'b1), .pin5(_74238_1_pin13),
    .pin6(_744075_2_pin11), .pin7(1'b0), .pin8(_744075_3_pin12), .pin9(_74238_1_pin13), .pin10(A0),
    .pin11(_744075_4_pin5), .pin12(_74238_1_pin12), .pin13(1'b1), .pin14(1'b1));
  _7408 _7408_7 (
    .pin1(A0), .pin2(_7408_2_pin2), .pin3(_744075_3_pin2), .pin4(A0), .pin5(_74238_1_pin12),
    .pin6(_744075_2_pin12), .pin7(1'b0), .pin8(_744075_3_pin13), .pin9(_74238_1_pin12), .pin10(1'b1),
    .pin11(_744075_4_pin3), .pin12(_7408_2_pin2), .pin13(1'b1), .pin14(1'b1));
  _7408 _7408_8 (
    .pin1(A0), .pin2(_7408_3_pin2), .pin3(_744075_2_pin2), .pin4(A0), .pin5(_7408_3_pin2),
    .pin6(_7432_1_pin5), .pin7(1'b0), .pin8(_744075_2_pin5), .pin9(1'b1), .pin10(_74238_1_pin12),
    .pin11(_744075_3_pin8), .pin12(_7408_3_pin2), .pin13(1'b1), .pin14(1'b1));
  _7408 _7408_9 (
    .pin1(A0), .pin2(_7408_4_pin2), .pin3(_744075_1_pin8), .pin4(A0), .pin5(_7408_4_pin2),
    .pin6(_744075_3_pin3), .pin7(1'b0), .pin8(_7432_1_pin4), .pin9(_7408_4_pin2), .pin10(1'b1),
    .pin11(_744075_2_pin8), .pin12(_7408_4_pin2), .pin13(1'b1), .pin14(1'b1));
  and and_4 (and_4_out, and_3_out, not_7_out);
  and and_5 (and_5_out, not_8_out, and_4_out);
  and and_6 (and_6_out, 1'b1, and_4_out);
  and and_7 (and_7_out, and_8_out, not_3_out);
  and and_8 (and_8_out, not_1_out, not_6_out);
  and and_9 (and_9_out, and_8_out, not_7_out);
  and and_10 (and_10_out, and_11_out, not_3_out);
  and and_11 (and_11_out, not_5_out, not_2_out);
  and and_12 (and_12_out, 1'b1, and_7_out);
  and and_13 (and_13_out, not_8_out, and_7_out);
  and and_14 (and_14_out, 1'b1, and_7_out);
  and and_15 (and_15_out, and_11_out, not_7_out);
  and and_16 (and_16_out, and_17_out, not_3_out);
  and and_17 (and_17_out, not_5_out, not_6_out);
  and and_18 (and_18_out, and_17_out, not_7_out);
  and and_19 (and_19_out, 1'b1, and_9_out);
  and and_20 (and_20_out, 1'b1, and_9_out);
  and and_21 (and_21_out, not_8_out, and_9_out);
  and and_22 (and_22_out, 1'b1, and_9_out);
  and and_23 (and_23_out, not_8_out, and_10_out);
  and and_24 (and_24_out, 1'b1, and_10_out);
  and and_25 (and_25_out, 1'b1, and_10_out);
  and and_26 (and_26_out, not_8_out, and_10_out);
  and and_27 (and_27_out, 1'b1, and_10_out);
  and and_28 (and_28_out, 1'b1, and_15_out);
  and and_29 (and_29_out, not_8_out, and_15_out);
  and and_30 (and_30_out, 1'b1, and_15_out);
  and and_31 (and_31_out, 1'b1, and_15_out);
  and and_32 (and_32_out, not_8_out, and_15_out);
  and and_33 (and_33_out, 1'b1, and_15_out);
  and and_34 (and_34_out, not_8_out, and_16_out);
  and and_35 (and_35_out, 1'b1, and_16_out);
  and and_36 (and_36_out, not_8_out, and_16_out);
  and and_37 (and_37_out, 1'b1, and_16_out);
  and and_38 (and_38_out, 1'b1, and_16_out);
  and and_39 (and_39_out, not_8_out, and_16_out);
  and and_40 (and_40_out, 1'b1, and_16_out);
  and and_41 (and_41_out, 1'b1, and_18_out);
  and and_42 (and_42_out, not_8_out, and_18_out);
  and and_43 (and_43_out, 1'b1, and_18_out);
  and and_44 (and_44_out, not_8_out, and_18_out);
  and and_45 (and_45_out, 1'b1, and_18_out);
  and and_46 (and_46_out, 1'b1, and_18_out);
  and and_47 (and_47_out, not_8_out, and_18_out);
  and and_48 (Out7, 1'b1, and_18_out);

  // Notes on the sheet:
  //   Out6
  //   Out7
  //   Out4
  //   Out5
  //   Out2
  //   Out3
  //   Out0
  //   Out1
  //   Bottom row=in, top row=out
  //   Bit 7
  //   bit6, bit3, bit1
  //   74HC4075 triple 3-input OR x4
  //   74HC32 quad 2-input OR x1
  //   74HC08 quad 2-input AND x9
  //   74HC238 3 to 8 decoder x1
endmodule
