// Digital circuit dac_decoder_old.dig as structural Verilog
module dac_decoder_old (
  input  A,
  input  B,
  input  C,
  input  D,
  input  InA,
  input  InB,
  input  InC,
  input  InD,
  output Out7,
  output Out6,
  output Out5,
  output Out4,
  output Out3,
  output Out2,
  output Out1,
  output Out0,
  output Bit0,
  output Bit1,
  output Bit2,
  output Bit3,
  output Bit4
);

  wire _7402_1_pin1, _7402_1_pin4, _7402_1_pin10, _7402_1_pin13, _7402_2_pin1, _7402_2_pin4, _7402_2_pin10,
       _7402_2_pin13, _7402_3_pin4, _7402_3_pin5, _7402_3_pin13, _7408_1_pin3, _7408_1_pin6, _7408_1_pin8,
       _7408_1_pin11, _7408_2_pin8, _7408_2_pin11, _7408_3_pin3, _7408_4_pin2, _7408_4_pin3, _7408_4_pin6,
       _7408_4_pin8, _7408_4_pin11, _7408_4_pin12, _7408_5_pin3, _7408_5_pin6, _7408_5_pin8, _7408_5_pin9,
       _7408_5_pin11, _7408_5_pin12, _7408_6_pin3, _7408_6_pin11, _7432_1_pin3, _7432_1_pin4, _7432_1_pin5,
       _7432_1_pin9, _7432_1_pin10, _7432_1_pin12, _7432_2_pin8, _7432_4_pin3, and_1_out, and_2_out,
       and_3_out, and_4_out, and_5_out, and_6_out, and_7_out, and_8_out, and_9_out, and_10_out, and_11_out,
       and_12_out, and_13_out, and_14_out, and_16_out, and_18_out, and_19_out, and_20_out, and_21_out,
       and_22_out, and_23_out, and_24_out, and_25_out, and_26_out, nor_1_out, nor_2_out, nor_3_out,
       nor_4_out, not_1_out, not_2_out, not_3_out, not_4_out, not_5_out, not_6_out, not_7_out, or_2_out,
       or_5_out, or_6_out, or_8_out, or_10_out, or_11_out, or_13_out, or_14_out, or_15_out;

  and and_1 (and_1_out, Out7, or_14_out);
  or or_1 (Out0, and_1_out, and_2_out);
  and and_2 (and_2_out, nor_4_out, not_1_out);
  not not_1 (not_1_out, nor_2_out);
  and and_3 (and_3_out, A, or_2_out);
  or or_2 (or_2_out, and_23_out, and_4_out);
  and and_4 (and_4_out, not_4_out, or_15_out);
  or or_3 (Out1, and_3_out, and_5_out);
  and and_5 (and_5_out, nor_2_out, D);
  or or_4 (Out2, and_6_out, and_7_out);
  and and_6 (and_6_out, and_18_out, D);
  and and_7 (and_7_out, nor_3_out, or_5_out);
  or or_5 (or_5_out, and_24_out, and_25_out);
  and and_8 (and_8_out, or_6_out, B);
  or or_6 (or_6_out, and_18_out, and_22_out);
  or or_7 (Out3, and_8_out, and_9_out);
  and and_9 (and_9_out, nor_1_out, not_2_out);
  not not_2 (not_2_out, and_26_out);
  and and_10 (and_10_out, or_8_out, and_26_out);
  or or_8 (or_8_out, Out7, nor_1_out);
  and and_11 (and_11_out, and_20_out, not_6_out);
  or or_9 (Out4, and_10_out, or_10_out);
  or or_10 (or_10_out, and_11_out, and_12_out);
  and and_12 (and_12_out, nor_2_out, B);
  and and_13 (and_13_out, or_11_out, B);
  or or_11 (or_11_out, and_19_out, and_21_out);
  or or_12 (Out5, and_13_out, and_14_out);
  and and_14 (and_14_out, and_20_out, or_15_out);
  and and_15 (Out6, A, or_13_out);
  or or_13 (or_13_out, and_23_out, and_16_out);
  and and_16 (and_16_out, not_4_out, or_14_out);
  not not_3 (not_3_out, A);
  not not_4 (not_4_out, B);
  not not_5 (not_5_out, C);
  not not_6 (not_6_out, D);
  and and_17 (Out7, A, B);
  and and_18 (and_18_out, A, C);
  and and_19 (and_19_out, A, D);
  and and_20 (and_20_out, A, not_4_out);
  and and_21 (and_21_out, not_3_out, C);
  and and_22 (and_22_out, not_3_out, D);
  nor nor_1 (nor_1_out, A, B);
  nor nor_2 (nor_2_out, A, C);
  nor nor_3 (nor_3_out, A, D);
  and and_23 (and_23_out, B, C);
  and and_24 (and_24_out, B, not_5_out);
  and and_25 (and_25_out, not_4_out, C);
  nor nor_4 (nor_4_out, B, D);
  and and_26 (and_26_out, C, D);
  or or_14 (or_14_out, C, D);
  or or_15 (or_15_out, and_26_out, not_7_out);
  not not_7 (not_7_out, or_14_out);
  _7402 _7402_1 (
    .pin1(_7402_1_pin1), .pin2(InA), .pin3(InA), .pin4(_7402_1_pin4), .pin5(InC), .pin6(InC), .pin7(1'b0),
    .pin8(InD), .pin9(InD), .pin10(_7402_1_pin10), .pin11(InB), .pin12(InB), .pin13(_7402_1_pin13),
    .pin14(1'b1));
  _7402 _7402_2 (
    .pin1(_7402_2_pin1), .pin2(InA), .pin3(InB), .pin4(_7402_2_pin4), .pin5(InA), .pin6(InD), .pin7(1'b0),
    .pin8(InD), .pin9(InB), .pin10(_7402_2_pin10), .pin11(InC), .pin12(InA), .pin13(_7402_2_pin13),
    .pin14(1'b1));
  _7408 _7408_1 (
    .pin1(InA), .pin2(InB), .pin3(_7408_1_pin3), .pin4(InA), .pin5(InD), .pin6(_7408_1_pin6), .pin7(1'b0),
    .pin8(_7408_1_pin8), .pin9(_7402_1_pin13), .pin10(InA), .pin11(_7408_1_pin11), .pin12(InC), .pin13(InA),
    .pin14(1'b1));
  _7432 _7432_1 (
    .pin1(InD), .pin2(InC), .pin3(_7432_1_pin3), .pin4(_7432_1_pin4), .pin5(_7432_1_pin5), .pin7(1'b0),
    .pin8(Bit0), .pin9(_7432_1_pin9), .pin10(_7432_1_pin10), .pin12(_7432_1_pin12), .pin13(_7408_1_pin6),
    .pin14(1'b1));  // open: pin6, pin11
  _7408 _7408_2 (
    .pin1(_7402_1_pin1), .pin2(InC), .pin3(_7432_1_pin12), .pin4(InB), .pin5(InC), .pin6(_7432_1_pin4),
    .pin7(1'b0), .pin8(_7408_2_pin8), .pin9(_7402_1_pin4), .pin10(InB), .pin11(_7408_2_pin11), .pin12(InD),
    .pin13(_7402_1_pin1), .pin14(1'b1));
  _7402 _7402_3 (
    .pin1(_7432_1_pin5), .pin2(_7432_1_pin3), .pin3(_7432_1_pin3), .pin4(_7402_3_pin4), .pin5(_7402_3_pin5),
    .pin6(_7402_3_pin5), .pin7(1'b0), .pin8(1'b0), .pin9(1'b0), .pin11(_7402_2_pin13), .pin12(_7402_2_pin13),
    .pin13(_7402_3_pin13), .pin14(1'b1));  // open: pin10
  _7408 _7408_3 (
    .pin1(_7402_1_pin13), .pin2(InC), .pin3(_7408_3_pin3), .pin4(_7408_1_pin3), .pin5(_7432_1_pin3),
    .pin6(_7432_1_pin10), .pin7(1'b0), .pin8(_7432_1_pin9), .pin9(_7402_3_pin13), .pin10(_7402_2_pin10),
    .pin11(_7402_3_pin5), .pin12(InD), .pin13(InC), .pin14(1'b1));
  _7408 _7408_4 (
    .pin1(_7402_1_pin13), .pin2(_7408_4_pin2), .pin3(_7408_4_pin3), .pin4(_7402_2_pin13), .pin5(InD),
    .pin6(_7408_4_pin6), .pin7(1'b0), .pin8(_7408_4_pin8), .pin9(InD), .pin10(_7408_1_pin11),
    .pin11(_7408_4_pin11), .pin12(_7408_4_pin12), .pin13(InA), .pin14(1'b1));
  _7432 _7432_2 (
    .pin1(_7432_1_pin4), .pin2(_7408_4_pin3), .pin3(_7408_4_pin12), .pin4(_7408_4_pin11),
    .pin5(_7408_4_pin6), .pin6(Bit1), .pin7(1'b0), .pin8(_7432_2_pin8), .pin9(_7408_3_pin3),
    .pin10(_7408_2_pin8), .pin11(_7408_4_pin2), .pin12(_7402_3_pin5), .pin13(_7432_1_pin5), .pin14(1'b1));
  _7408 _7408_5 (
    .pin1(_7402_2_pin4), .pin2(_7432_2_pin8), .pin3(_7408_5_pin3), .pin4(_7402_3_pin4), .pin5(_7402_2_pin1),
    .pin6(_7408_5_pin6), .pin7(1'b0), .pin8(_7408_5_pin8), .pin9(_7408_5_pin9), .pin10(_7402_3_pin5),
    .pin11(_7408_5_pin11), .pin12(_7408_5_pin12), .pin13(InB), .pin14(1'b1));
  _7432 _7432_3 (
    .pin1(_7408_4_pin8), .pin2(_7408_5_pin3), .pin3(Bit2), .pin4(_7408_5_pin11), .pin5(_7408_5_pin6),
    .pin6(Bit3), .pin7(1'b0), .pin8(_7408_5_pin9), .pin9(_7402_2_pin1), .pin10(_7408_1_pin3),
    .pin11(_7408_5_pin12), .pin12(_7408_2_pin11), .pin13(_7408_1_pin11), .pin14(1'b1));
  _7408 _7408_6 (
    .pin1(_7408_1_pin8), .pin2(_7402_1_pin10), .pin3(_7408_6_pin3), .pin4(1'b0), .pin5(1'b0), .pin7(1'b0),
    .pin9(1'b0), .pin10(1'b0), .pin11(_7408_6_pin11), .pin12(InB), .pin13(_7402_2_pin13), .pin14(1'b1));  // open: pin6, pin8
  _7432 _7432_4 (
    .pin1(_7408_5_pin8), .pin2(_7408_6_pin3), .pin3(_7432_4_pin3), .pin4(1'b0), .pin5(1'b0), .pin7(1'b0),
    .pin9(1'b0), .pin10(1'b0), .pin11(Bit4), .pin12(_7408_6_pin11), .pin13(_7432_4_pin3), .pin14(1'b1));  // open: pin6, pin8

  // Notes on the sheet:
  //   4x 7432
  //   7x 7408
  //   3x 7402
  //   (2 7402s replace 2 7404s)
  //   15 OR gates
  //   27 AND gates
  //   4 NOR gates
  //   7 inverters
  //   Bit 3
  //   Bit 0
  //   ab
  //   ac
  //   ad
  //   ab'
  //   a'c
  //   a'd
  //   a'b'
  //   a'c'
  //   a'd'
  //   bc
  //   bc'
  //   b'c
  //   b'd'
  //   cd
  //   c+d
  //   d'
  //   b'
  //   (c+d)'
  //   acd
  //   cd+(c+d)'
  //   cd(ab+a'b')
endmodule
